// Logisim project 24H_Format_Clock.circ as structural Verilog: 6 circuits, main circuit main
module main (
  input  Load,
  input  Clock,
  input  Clear,
  input  Count,
  input  [1:0] in_5,
  input  [3:0] in_6,
  input  [3:0] in_7,
  input  [3:0] in_8,
  input  [3:0] in_9,
  input  [3:0] in_10
);

  wire clock_1_out, MM_next_clock, SS_next_clock;
  wire [3:0] HH_lsb, HH_msb, MM_lsb, MM_msb, SS_lsb, SS_msb;

  Clock clock_1 (.out(clock_1_out));
  Hex_Digit_Display hex_digit_display_1 (.value(HH_msb));  // open: dp
  _0_23_counter_load HH (
    .Load_One_s_Place(in_5), .Load_Ten_s_Place(in_6), .Load(Load), .Count(MM_next_clock),
    .Clock(clock_1_out), .Clear(Clear), .MSB(HH_msb), .LSB(HH_lsb));
  Hex_Digit_Display hex_digit_display_2 (.value(HH_lsb));  // open: dp
  Hex_Digit_Display hex_digit_display_3 (.value(MM_msb));  // open: dp
  Hex_Digit_Display hex_digit_display_4 (.value(MM_lsb));  // open: dp
  _0_59_count_load MM (
    .Load_Ten_s_Place(in_7), .Load_One_s_Place(in_8), .Load(Load), .Count(SS_next_clock),
    .Clock(clock_1_out), .Clear(Clear), .MSB(MM_msb), .LSB(MM_lsb), .Next_Clock(MM_next_clock));
  Hex_Digit_Display hex_digit_display_5 (.value(SS_msb));  // open: dp
  Hex_Digit_Display hex_digit_display_6 (.value(SS_lsb));  // open: dp
  _0_59_count_load SS (
    .Load_Ten_s_Place(in_9), .Load_One_s_Place(in_10), .Load(Load), .Count(Count), .Clock(clock_1_out),
    .Clear(Clear), .MSB(SS_msb), .LSB(SS_lsb), .Next_Clock(SS_next_clock));
endmodule

module decade_with_parallel_load (
  input  Count,
  input  Load,
  input  [3:0] Load_Value,
  input  Clock,
  input  Clear,
  output [3:0] out_6,
  output A0,
  output A1,
  output A2,
  output A3
);

  wire _0_qn, _2_qn, and_1_out, and_2_out, and_3_out, and_4_out, and_5_out, and_6_out, and_7_out, and_8_out,
       and_9_out, and_10_out, and_11_out, and_12_out, and_13_out, not_1_out, not_2_out, not_3_out, not_4_out,
       not_5_out, or_1_out, or_2_out, or_3_out, or_4_out, or_5_out, or_6_out, or_7_out, or_8_out, or_9_out;

  not not_1 (not_1_out, Load);
  not not_2 (not_2_out, Load_Value[3]);
  and and_1 (and_1_out, Count, not_1_out);
  not not_3 (not_3_out, Load_Value[0]);
  not not_4 (not_4_out, Load_Value[1]);
  not not_5 (not_5_out, Load_Value[2]);
  and and_2 (and_2_out, Load, Load_Value[0]);
  and and_3 (and_3_out, Load, not_3_out);
  and and_4 (and_4_out, Load_Value[1], Load);
  and and_5 (and_5_out, not_4_out, Load);
  and and_6 (and_6_out, Load_Value[2], Load);
  and and_7 (and_7_out, Load, not_5_out);
  and and_8 (and_8_out, Load_Value[3], Load);
  and and_9 (and_9_out, Load, not_2_out);
  or or_1 (or_1_out, Clear, and_13_out);
  and and_10 (and_10_out, and_1_out, A0);
  and and_11 (and_11_out, and_1_out, A0, A1);
  and and_12 (and_12_out, and_1_out, A0, A1, A2);
  or or_2 (or_2_out, and_2_out, and_1_out);
  or or_3 (or_3_out, and_3_out, and_1_out);
  or or_4 (or_4_out, and_4_out, and_10_out);
  or or_5 (or_5_out, and_10_out, and_5_out);
  or or_6 (or_6_out, and_6_out, and_11_out);
  or or_7 (or_7_out, and_11_out, and_7_out);
  or or_8 (or_8_out, and_8_out, and_12_out);
  or or_9 (or_9_out, and_12_out, and_9_out);
  J_K_Flip_Flop _0 (.J(or_2_out), .clk(Clock), .K(or_3_out), .Q(A0), .Qn(_0_qn), .reset(or_1_out));  // open: preset, en
  and and_13 (and_13_out, A3, _2_qn, A1, _0_qn);
  J_K_Flip_Flop _1 (.J(or_4_out), .clk(Clock), .K(or_5_out), .Q(A1), .reset(or_1_out));  // open: Qn, preset, en
  J_K_Flip_Flop _2 (.J(or_6_out), .clk(Clock), .K(or_7_out), .Q(A2), .Qn(_2_qn), .reset(or_1_out));  // open: preset, en
  J_K_Flip_Flop _3 (.J(or_8_out), .clk(Clock), .K(or_9_out), .Q(A3), .reset(or_1_out));  // open: Qn, preset, en
  Hex_Digit_Display hex_digit_display_1 (.value({A3, A2, A1, A0}));  // open: dp

  assign out_6 = {A3, A2, A1, A0};
endmodule

module _0_59_count_load (
  input  [3:0] Load_Ten_s_Place,
  input  [3:0] Load_One_s_Place,
  input  Load,
  input  Count,
  input  Clock,
  input  Clear,
  output [3:0] MSB,
  output [3:0] LSB,
  output Next_Clock
);

  wire _0_prime_out, _6_prime_2_out, _6_prime_out, and_1_out, and_2_out, decade_with_parallel_load_1_a0,
       decade_with_parallel_load_1_a1, decade_with_parallel_load_1_a2, decade_with_parallel_load_1_a3,
       decade_with_parallel_load_2_a0, decade_with_parallel_load_2_a1, decade_with_parallel_load_2_a2,
       decade_with_parallel_load_2_a3, not_1_out, not_2_out, not_3_out, not_4_out, not_5_out, not_6_out,
       not_7_out, or_1_out;

  or or_1 (or_1_out, Clear, and_1_out);
  and and_1 (and_1_out, _0_prime_out, _6_prime_out);
  decade_with_parallel_load decade_with_parallel_load_1 (
    .Count(Count), .Load(Load), .Load_Value(Load_One_s_Place), .Clock(Clock), .Clear(or_1_out), .out_6(LSB),
    .A0(decade_with_parallel_load_1_a0), .A1(decade_with_parallel_load_1_a1),
    .A2(decade_with_parallel_load_1_a2), .A3(decade_with_parallel_load_1_a3));
  and _0_prime (_0_prime_out, not_1_out, not_2_out, not_3_out, not_4_out);
  not not_1 (not_1_out, decade_with_parallel_load_1_a3);
  not not_2 (not_2_out, decade_with_parallel_load_1_a2);
  not not_3 (not_3_out, decade_with_parallel_load_1_a1);
  not not_4 (not_4_out, decade_with_parallel_load_1_a0);
  and _6_prime (_6_prime_out, not_5_out, decade_with_parallel_load_2_a2, decade_with_parallel_load_2_a1, not_6_out);
  and and_2 (and_2_out, decade_with_parallel_load_1_a3, not_3_out, Count, not_2_out, decade_with_parallel_load_1_a0);
  not not_5 (not_5_out, decade_with_parallel_load_2_a3);
  not not_6 (not_6_out, decade_with_parallel_load_2_a0);
  decade_with_parallel_load decade_with_parallel_load_2 (
    .Count(and_2_out), .Load(Load), .Load_Value(Load_Ten_s_Place), .Clock(Clock), .Clear(or_1_out),
    .out_6(MSB), .A0(decade_with_parallel_load_2_a0), .A1(decade_with_parallel_load_2_a1),
    .A2(decade_with_parallel_load_2_a2), .A3(decade_with_parallel_load_2_a3));
  Hex_Digit_Display hex_digit_display_1 (.value(LSB));  // open: dp
  Hex_Digit_Display hex_digit_display_2 (.value(MSB));  // open: dp
  not not_7 (not_7_out, decade_with_parallel_load_2_a1);
  and _6_prime_2 (_6_prime_2_out, decade_with_parallel_load_2_a0, not_7_out, decade_with_parallel_load_2_a2, not_5_out);
  and and_3 (Next_Clock, and_2_out, Count, _6_prime_2_out);
endmodule

module _0_23_counter_load (
  input  [1:0] Load_One_s_Place,
  input  [3:0] Load_Ten_s_Place,
  input  Load,
  input  Count,
  input  Clock,
  input  Clear,
  output [3:0] MSB,
  output [3:0] LSB
);

  wire _4_prime_2_out, _4_prime_out, and_1_out, and_2_out, decade_with_parallel_load_1_a0,
       decade_with_parallel_load_1_a1, decade_with_parallel_load_1_a2, decade_with_parallel_load_1_a3,
       mod_3_counter_load_1_a0, mod_3_counter_load_1_a1, mod_3_counter_load_1_a2, mod_3_counter_load_1_a3,
       not_1_out, not_2_out, not_3_out, not_4_out, not_5_out, not_6_out, not_7_out, or_1_out;

  or or_1 (or_1_out, Clear, and_1_out);
  and and_1 (and_1_out, _4_prime_out, _4_prime_2_out);
  decade_with_parallel_load decade_with_parallel_load_1 (
    .Count(Count), .Load(Load), .Load_Value(Load_Ten_s_Place), .Clock(Clock), .Clear(or_1_out), .out_6(LSB),
    .A0(decade_with_parallel_load_1_a0), .A1(decade_with_parallel_load_1_a1),
    .A2(decade_with_parallel_load_1_a2), .A3(decade_with_parallel_load_1_a3));
  and _4_prime (_4_prime_out, not_1_out, decade_with_parallel_load_1_a2, not_2_out, not_3_out);
  not not_1 (not_1_out, decade_with_parallel_load_1_a3);
  not not_2 (not_2_out, decade_with_parallel_load_1_a1);
  not not_3 (not_3_out, decade_with_parallel_load_1_a0);
  and _4_prime_2 (_4_prime_2_out, not_5_out, not_6_out, mod_3_counter_load_1_a1, not_7_out);
  not not_4 (not_4_out, decade_with_parallel_load_1_a2);
  not not_5 (not_5_out, mod_3_counter_load_1_a3);
  and and_2 (and_2_out, decade_with_parallel_load_1_a3, not_4_out, Count, decade_with_parallel_load_1_a0, not_2_out);
  not not_6 (not_6_out, mod_3_counter_load_1_a2);
  not not_7 (not_7_out, mod_3_counter_load_1_a0);
  Mod_3_counter_Load mod_3_counter_load_1 (
    .Count(and_2_out), .Load(Load), .Load_Value(Load_One_s_Place), .Clock(Clock), .Clear(or_1_out),
    .Hex(MSB), .A0(mod_3_counter_load_1_a0), .A1(mod_3_counter_load_1_a1), .A2(mod_3_counter_load_1_a2),
    .A3(mod_3_counter_load_1_a3));
  Hex_Digit_Display hex_digit_display_1 (.value(MSB));  // open: dp
  Hex_Digit_Display hex_digit_display_2 (.value(LSB));  // open: dp
endmodule

module Mod_3_counter_Load (
  input  Count,
  input  Load,
  input  [1:0] Load_Value,
  input  Clock,
  input  Clear,
  output [3:0] Hex,
  output A0,
  output A1,
  output A2,
  output A3
);

  wire and_1_out, and_2_out, and_3_out, and_4_out, and_5_out, and_6_out, and_7_out, not_1_out, not_2_out,
       not_3_out, or_1_out, or_2_out, or_3_out, or_4_out, or_5_out;

  not not_1 (not_1_out, Load);
  and and_1 (and_1_out, Count, not_1_out);
  not not_2 (not_2_out, Load_Value[0]);
  not not_3 (not_3_out, Load_Value[1]);
  and and_2 (and_2_out, Load, Load_Value[0]);
  and and_3 (and_3_out, Load, not_2_out);
  and and_4 (and_4_out, Load_Value[1], Load);
  and and_5 (and_5_out, not_3_out, Load);
  or or_1 (or_1_out, Clear, and_7_out);
  and and_6 (and_6_out, and_1_out, A0);
  or or_2 (or_2_out, and_2_out, and_1_out);
  or or_3 (or_3_out, and_3_out, and_1_out);
  or or_4 (or_4_out, and_4_out, and_6_out);
  or or_5 (or_5_out, and_6_out, and_5_out);
  J_K_Flip_Flop _0 (.J(or_2_out), .clk(Clock), .K(or_3_out), .Q(A0), .reset(or_1_out));  // open: Qn, preset, en
  and and_7 (and_7_out, A1, A0);
  J_K_Flip_Flop _1 (.J(or_4_out), .clk(Clock), .K(or_5_out), .Q(A1), .reset(or_1_out));  // open: Qn, preset, en
  Hex_Digit_Display hex_digit_display_1 (.value({2'b00, A1, A0}));  // open: dp

  assign A2 = 1'b0;
  assign A3 = 1'b0;
  assign Hex = {2'b00, A1, A0};
endmodule

module _24H_Clock (
  input  Load,
  input  Clock,
  input  Clear,
  input  Count,
  input  [1:0] in_5,
  input  [3:0] in_6,
  input  [3:0] in_7,
  input  [3:0] in_8,
  input  [3:0] in_9,
  input  [3:0] in_10
);

  wire clock_1_out, MM_next_clock, SS_next_clock;
  wire [3:0] HH_lsb, HH_msb, MM_lsb, MM_msb, SS_lsb, SS_msb;

  Clock clock_1 (.out(clock_1_out));
  Hex_Digit_Display hex_digit_display_1 (.value(HH_msb));  // open: dp
  _0_23_counter_load HH (
    .Load_One_s_Place(in_5), .Load_Ten_s_Place(in_6), .Load(Load), .Count(MM_next_clock),
    .Clock(clock_1_out), .Clear(Clear), .MSB(HH_msb), .LSB(HH_lsb));
  Hex_Digit_Display hex_digit_display_2 (.value(HH_lsb));  // open: dp
  Hex_Digit_Display hex_digit_display_3 (.value(MM_msb));  // open: dp
  Hex_Digit_Display hex_digit_display_4 (.value(MM_lsb));  // open: dp
  _0_59_count_load MM (
    .Load_Ten_s_Place(in_7), .Load_One_s_Place(in_8), .Load(Load), .Count(SS_next_clock),
    .Clock(clock_1_out), .Clear(Clear), .MSB(MM_msb), .LSB(MM_lsb), .Next_Clock(MM_next_clock));
  Hex_Digit_Display hex_digit_display_5 (.value(SS_lsb));  // open: dp
  Hex_Digit_Display hex_digit_display_6 (.value(SS_msb));  // open: dp
  _0_59_count_load SS (
    .Load_Ten_s_Place(in_9), .Load_One_s_Place(in_10), .Load(Load), .Count(Count), .Clock(clock_1_out),
    .Clear(Clear), .MSB(SS_msb), .LSB(SS_lsb), .Next_Clock(SS_next_clock));
endmodule
