// Logisim project Traffic Sysytem.circ as structural Verilog: 1 circuit, main circuit main
module main (
);

  LED led_1 ();  // open: in
  LED led_2 ();  // open: in
  LED Right_Turn ();  // open: in
  LED Red ();  // open: in
  LED Green ();  // open: in
  LED Green_2 ();  // open: in
  LED Red_2 ();  // open: in
  LED Right_Turn_2 ();  // open: in
  LED Right_Turn_3 ();  // open: in
  LED Red_3 ();  // open: in
  LED Green_3 ();  // open: in
  LED Right_Turn_4 ();  // open: in
  LED Red_4 ();  // open: in
  LED Green_4 ();  // open: in
endmodule
